# Fritzing sketch Final Circuit (saved by Fritzing 0.9.3b)
stripboards: 2

parts:
  Part1 = Arduino Uno (Rev3)
  OLED_I2C1 = OLED 128x64 I2C Monochrome Display
  Gizwits_WiFi_Witty_ESP-12F1 = Gizwits WiFi Witty ESP-12F
  R1 = PHOTOCELL [package=photocell-kit]
  R2 = Temperature Sensor (Thermistor) [thermistor_type=NTC package=THT]
  Part2 = Soil Moisture Sensor
  LED1 = smd LED [color="Blue (525nm)" package="0603 [SMD]"]
  R3 = Resistor [tolerance=±5% resistance=10k package=THT]
  R4 = Resistor [tolerance=±5% resistance=10k package="2010 [SMD]"]
  R5 = Resistor [tolerance=±5% resistance=220 package="2010 [SMD]"]

nets:
  N1: Part1.A0, Part2.SIG
  N2: Part1.A2, R1.P$1, R4.Pin_1
  N3: Part1.A3, R2.pin_1, R3.Pin_1
  N4: Part1.A4/SDA, OLED_I2C1.SDA
  N5: Part1.A5/SCL, OLED_I2C1.SCK
  N6: Part1.D8, Gizwits_WiFi_Witty_ESP-12F1.REST
  N7: Part1.D13/SCK, R5.Pin_0
  GND: Part1.GND, OLED_I2C1.GND, Gizwits_WiFi_Witty_ESP-12F1.GND, Part2.GND, LED1.cathode, R3.Pin_0, R4.Pin_0
  3V3: Part1.AREF, Part1.3V3, Gizwits_WiFi_Witty_ESP-12F1.CH_PD, Gizwits_WiFi_Witty_ESP-12F1.VCC, R2.pin_0
  N8: Part1.D6_PWM, Gizwits_WiFi_Witty_ESP-12F1.TXD
  N9: Part1.D7, Gizwits_WiFi_Witty_ESP-12F1.RXD
  5V: Part1.5V, OLED_I2C1.VDD, R1.P$2, Part2.VCC
